# Fritzing sketch Sketch (saved by Fritzing 0.9.0b)
circuit board: 8.57561cm x 5.79527cm
breadboards: 1

parts:
  C1 = Electrolytic Capacitor [capacitance=4.7mF voltage=35V package="100 mil [THT, electrolytic]"]
  C2 = Electrolytic Capacitor [capacitance=4.7mF voltage=35V package="100 mil [THT, electrolytic]"]
  Q1 = Basic FET N-Channel [package="DPak [SMD]"]
  L1 = Inductor [package="1206 [SMD]"]
  D1 = DIODE-SCHOTTKY [package=sma-diode]
  U1 = Voltage Regulator - 5V [package="DPak [SMD]"]
  C3 = Ceramic Capacitor [capacitance=100nF package="100 mil [THT, multilayer]"]
  C4 = Ceramic Capacitor [capacitance=100nF package="100 mil [THT, multilayer]"]
  R1 = Resistor [tolerance=±5% resistance=220 package=THT]

nets:
  N1: C1.-, Q1.drain, U1.GND, C3.0, C4.0
  N2: C1.+, L1.pin_0, D1.C
  N3: C2.-, Q1.source, D1.A
  N4: C2.+, L1.pin_1
  N5: Q1.Gate, R1.Pin_0
  N6: U1.input_voltage, C3.1
  N7: U1.output_voltage, C4.1
